# Fritzing sketch AndroidThings-PIR (saved by Fritzing 0.9.3b)
breadboards: 1

parts:
  Raspberry_Pi_1 = Raspberry Pi 3 [part_number=RPI-3-V1.2]
  PIR2 = PIR sensor
  R1 = Resistor [tolerance=±5% resistance=330 package="0603 [SMD]"]
  LED1 = smd LED [color="Red (633nm)" package="0805 [SMD]"]

nets:
  N1: Raspberry_Pi_1.GIPO6, PIR2.SIG, R1.Pin_0
  GND: Raspberry_Pi_1.GND, PIR2.GND, LED1.cathode
  N2: R1.Pin_1, LED1.anode
